// Digital circuit Register_File.dig as structural Verilog
module Register_File (
  input  Clk,
  input  [3:0] Write_Data,
  input  [1:0] Write_Register,
  input  [7:0] Ctrl_Registers,
  input  [1:0] Read_Register1,
  input  [1:0] Read_Register2,
  output [3:0] Read_Data1,
  output [3:0] Read_Data2
);

  wire [3:0] demultiplexer_1_out_0, demultiplexer_1_out_1, demultiplexer_1_out_2, demultiplexer_1_out_3,
       R0_p4, R1_p4, R2_p4, R3_p4;

  Demultiplexer #(.Selector_Bits(2), .Bits(4)) demultiplexer_1 (
    .sel(Write_Register), .in(Write_Data), .out_0(demultiplexer_1_out_0), .out_1(demultiplexer_1_out_1),
    .out_2(demultiplexer_1_out_2), .out_3(demultiplexer_1_out_3));
  // _4_bit_GPR R3: pin names not known; wires that end beside it: demultiplexer_1_out_3, Clk, Ctrl_Registers[1:0], R3_p4
  // _4_bit_GPR R2: pin names not known; wires that end beside it: demultiplexer_1_out_2, Clk, Ctrl_Registers[3:2], R2_p4
  // _4_bit_GPR R1: pin names not known; wires that end beside it: demultiplexer_1_out_1, Clk, Ctrl_Registers[5:4], R1_p4
  // _4_bit_GPR R0: pin names not known; wires that end beside it: demultiplexer_1_out_0, Clk, Ctrl_Registers[7:6], R0_p4
  Multiplexer #(.Selector_Bits(2), .Bits(4)) multiplexer_1 (
    .sel(Read_Register1), .in_0(R0_p4), .in_1(R1_p4), .in_2(R2_p4), .in_3(R3_p4), .out(Read_Data1));
  Multiplexer #(.Selector_Bits(2), .Bits(4)) multiplexer_2 (
    .sel(Read_Register2), .in_0(R0_p4), .in_1(R1_p4), .in_2(R2_p4), .in_3(R3_p4), .out(Read_Data2));
endmodule
